# Fritzing sketch Fingerhackccess (saved by Fritzing 0.9.3b)
breadboards: 1

parts:
  U1 = NodeMCU V1.0
  U2 = LCD-16X2 [package=lcd-16x2_noholes]
  LCM1602_IIC1 = LCM1602 IIC [part_number="LCM1602 IIC" chip_label="LCM1602 IIC" package="DIP (Dual Inline) [THT]"]
  M1 = RioRand LM2596
  M2 = RioRand LM2596
  Componente1 = Logic Level Converter
  Componente2 = sensor_biometrico
  ZS-042_RTC1 = ZS-042 RTC Module
  DHT1 = DHT22 Humidity and Temperature Sensor
  J1 = Power Jack [package=power_jack_smd]
  U3 = CAPSENSE_PAD [package=capsense_pad]
  R1 = Resistor [tolerance=±5% resistance=1k package="0402 [SMD]"]

nets:
  N1: U1.D1, Componente1.RX2_HV
  N2: U1.D2, Componente1.TX2_HV
  N3: U1.D3, DHT1.DATA, R1.Pin_1
  N4: U1.3V3, M2.Pin_3, Componente1.LV
  GND: U1.GND, M1.Pin_4, M2.Pin_4, Componente1.GND, Componente2.GND, ZS-042_RTC1.GND#0, DHT1.GND
  N5: U1.D5, Componente1.RX_HV
  N6: U1.D6, Componente1.TX_HV
  N7: U1.D7, U3.RECEIVE
  N8: U1.D8, U3.RES
  VSS: U2.VSS, LCM1602_IIC1.VSS
  VDD: U2.VDD, LCM1602_IIC1.VDD
  N9: U2.VO, LCM1602_IIC1.V0
  N10: U2.RS, LCM1602_IIC1.RS
  N11: U2.R_W, LCM1602_IIC1.RW
  N12: U2.E, LCM1602_IIC1.E
  N13: U2.DB0, LCM1602_IIC1.D0
  N14: U2.DB1, LCM1602_IIC1.D1
  N15: U2.DB2, LCM1602_IIC1.D2
  N16: U2.DB3, LCM1602_IIC1.D3
  N17: U2.DB4, LCM1602_IIC1.D4
  N18: U2.DB5, LCM1602_IIC1.D5
  N19: U2.DB6, LCM1602_IIC1.D6
  N20: U2.DB7, LCM1602_IIC1.D7
  N21: U2.A, LCM1602_IIC1.A
  N22: U2.K, LCM1602_IIC1.K
  N23: LCM1602_IIC1.GND, ZS-042_RTC1.GND#6
  N24: LCM1602_IIC1.VCC, ZS-042_RTC1.VCC#7
  N25: LCM1602_IIC1.SDA, ZS-042_RTC1.SDA#8
  N26: LCM1602_IIC1.SCL, ZS-042_RTC1.SCL#9
  N27: LCM1602_IIC1.LED_A, LCM1602_IIC1.LED_B
  N28: M1.Pin_1, M2.Pin_1, J1.GNDBREAK
  N29: M1.Pin_2, M2.Pin_2, J1.GND
  VCC: M1.Pin_3, Componente1.HV, Componente2.VCC, ZS-042_RTC1.VCC#1, DHT1.VDD, R1.Pin_0
  N30: Componente1.TX2_LV, ZS-042_RTC1.SCL#3
  N31: Componente1.RX2_LV, ZS-042_RTC1.SDA#2
  N32: Componente1.RX_LV, Componente2.RX
  N33: Componente1.TX_LV, Componente2.TX

notes:
  5v
  3.3v
  Pull Up resistor ->
  Capacitive sensor

custom parts:
  NodeMCU V1.0: ESP8266 based NodeMCU
  LCM1602 IIC: I2C-Module to use a 1602 or 2004 LCD on with the wire.h libory Serial LCD Modul
  sensor_biometrico: Adafruit Optical Fingerprint Sensor
